// Logisim project SP1_COMPUTER.circ as structural Verilog
module DecoderInstruct (
  input  in_1,
  input  in_2,
  input  in_3,
  input  in_4,
  output out_5,
  output out_6,
  output out_7,
  output out_8,
  output out_9
);

  wire not_1_out, not_2_out, not_3_out, not_4_out;

  not not_1 (not_1_out, in_2);
  not not_2 (not_2_out, in_1);
  not not_3 (not_3_out, in_3);
  not not_4 (not_4_out, in_4);
  and and_1 (out_5, not_4_out, not_3_out, not_1_out, not_2_out);
  and and_2 (out_6, in_4, not_3_out, not_1_out, not_2_out);
  and and_3 (out_7, not_4_out, in_3, not_1_out, not_2_out);
  and and_4 (out_8, in_4, in_3, not_1_out, not_2_out);
  nand nand_1 (out_9, in_4, in_3, in_2, in_1);

  // Notes on the sheet:
  //   LDA
  //   ADD
  //   SUB
  //   OUT
  //   \HLT
endmodule

module DringCounter (
  input  CLK,
  input  nCLR,
  output T1,
  output T2,
  output T3,
  output T4,
  output T5,
  output T6
);

  wire not_1_out, not_2_out, not_3_out, not_4_out, not_5_out, not_6_out, not_7_out, not_8_out, not_9_out,
       not_10_out, not_11_out, not_12_out;

  not not_1 (not_1_out, CLK);
  not not_2 (not_2_out, nCLR);
  D_Flip_Flop d_ff_1 (.clk(not_1_out), .D(T6), .Q(T1), .preset(not_2_out));  // open: Qn, en, reset
  not not_3 (not_3_out, CLK);
  D_Flip_Flop d_ff_2 (.clk(not_3_out), .D(T1), .Q(T2), .reset(not_4_out));  // open: Qn, preset, en
  not not_4 (not_4_out, nCLR);
  D_Flip_Flop d_ff_3 (.clk(not_5_out), .D(T2), .Q(T3), .reset(not_6_out));  // open: Qn, preset, en
  not not_5 (not_5_out, CLK);
  not not_6 (not_6_out, nCLR);
  not not_7 (not_7_out, CLK);
  not not_8 (not_8_out, CLK);
  D_Flip_Flop d_ff_4 (.clk(not_7_out), .D(T3), .Q(T4), .reset(not_9_out));  // open: Qn, preset, en
  not not_9 (not_9_out, nCLR);
  D_Flip_Flop d_ff_5 (.clk(not_8_out), .D(T4), .Q(T5), .reset(not_10_out));  // open: Qn, preset, en
  not not_10 (not_10_out, nCLR);
  D_Flip_Flop d_ff_6 (.clk(not_11_out), .D(T5), .Q(T6), .reset(not_12_out));  // open: Qn, preset, en
  not not_11 (not_11_out, CLK);
  not not_12 (not_12_out, nCLR);
endmodule

module ControlMatrix (
  input  in_1,
  input  in_2,
  input  I4,
  input  I3,
  input  I2,
  input  I1,
  output out_7,
  output Cp,
  output Ep,
  output nLm,
  output nCe,
  output nLi,
  output nEi,
  output nLa,
  output Ea,
  output Su,
  output Eu,
  output nLb,
  output nLo
);

  wire c39_1_out_9, c39_1_out_10, c39_1_out_11, c39_1_out_12, c39_2_out_9, c39_2_out_10, c39_2_out_11,
       c39_2_out_12, c39_3_out_9, c39_3_out_10, c39_3_out_11, c39_3_out_12, c39_4_out_9, c39_4_out_10,
       c39_4_out_11, c39_4_out_12, c43_1_out_7, c43_1_out_8, c46_1_out_6, decoderinstruct_1_out_5,
       decoderinstruct_1_out_6, decoderinstruct_1_out_7, decoderinstruct_1_out_8, dringcounter_1_t3,
       dringcounter_1_t4, dringcounter_1_t5, dringcounter_1_t6, not_1_out, not_2_out;

  DecoderInstruct decoderinstruct_1 (
    .out_5(decoderinstruct_1_out_5), .out_6(decoderinstruct_1_out_6), .out_7(decoderinstruct_1_out_7),
    .out_8(decoderinstruct_1_out_8), .out_9(out_7), .in_1(I4), .in_2(I3), .in_3(I2), .in_4(I1));
  DringCounter dringcounter_1 (
    .CLK(in_1), .nCLR(in_2), .T1(Ep), .T2(Cp), .T3(dringcounter_1_t3), .T4(dringcounter_1_t4),
    .T5(dringcounter_1_t5), .T6(dringcounter_1_t6));
  not not_1 (not_1_out, Ep);
  C39 c39_1 (
    .in_1(decoderinstruct_1_out_5), .in_2(dringcounter_1_t4), .in_3(decoderinstruct_1_out_6),
    .in_4(dringcounter_1_t4), .in_5(decoderinstruct_1_out_7), .in_6(dringcounter_1_t4),
    .in_7(decoderinstruct_1_out_5), .in_8(dringcounter_1_t3), .out_9(c39_1_out_9), .out_10(c39_1_out_10),
    .out_11(c39_1_out_11), .out_12(c39_1_out_12));
  not not_2 (not_2_out, dringcounter_1_t3);
  C44 C44 (
    .in_1(not_1_out), .in_2(c39_1_out_9), .in_3(c39_1_out_10), .in_4(c39_1_out_11), .in_5(not_2_out),
    .in_6(c39_1_out_12), .in_7(c39_2_out_9), .in_8(c39_2_out_10), .out_9(nLm), .out_10(nCe));
  C39 c39_2 (
    .in_1(decoderinstruct_1_out_6), .in_2(dringcounter_1_t3), .in_3(decoderinstruct_1_out_7),
    .in_4(dringcounter_1_t5), .in_5(decoderinstruct_1_out_5), .in_6(dringcounter_1_t4),
    .in_7(decoderinstruct_1_out_6), .in_8(dringcounter_1_t4), .out_9(c39_2_out_9), .out_10(c39_2_out_10),
    .out_11(c39_2_out_11), .out_12(c39_2_out_12));
  not not_3 (nLi, dringcounter_1_t3);
  C45 c45_1 (
    .in_1(c39_2_out_11), .in_2(c39_2_out_12), .in_3(c39_3_out_9), .in_4(c39_3_out_10), .in_5(c39_3_out_11),
    .in_6(c39_3_out_12), .out_7(nEi), .out_8(nLa));
  C39 c39_3 (
    .in_1(decoderinstruct_1_out_7), .in_2(dringcounter_1_t4), .in_3(decoderinstruct_1_out_5),
    .in_4(dringcounter_1_t5), .in_5(decoderinstruct_1_out_6), .in_6(dringcounter_1_t6),
    .in_7(decoderinstruct_1_out_7), .in_8(dringcounter_1_t6), .out_9(c39_3_out_9), .out_10(c39_3_out_10),
    .out_11(c39_3_out_11), .out_12(c39_3_out_12));
  not not_4 (Ea, c39_4_out_9);
  C39 c39_4 (
    .in_1(decoderinstruct_1_out_8), .in_2(dringcounter_1_t4), .in_3(decoderinstruct_1_out_7),
    .in_4(dringcounter_1_t6), .in_5(decoderinstruct_1_out_6), .in_6(dringcounter_1_t6),
    .in_7(decoderinstruct_1_out_7), .in_8(dringcounter_1_t6), .out_9(c39_4_out_9), .out_10(c39_4_out_10),
    .out_11(c39_4_out_11), .out_12(c39_4_out_12));
  not not_5 (Su, c39_4_out_10);
  C46 c46_1 (
    .in_1(c39_4_out_11), .in_2(c39_4_out_12), .in_3(c43_1_out_7), .in_4(c43_1_out_8), .out_5(Eu),
    .out_6(c46_1_out_6));
  not not_6 (nLb, c46_1_out_6);
  C43 c43_1 (
    .in_1(decoderinstruct_1_out_6), .in_2(dringcounter_1_t5), .in_3(decoderinstruct_1_out_7),
    .in_4(dringcounter_1_t5), .in_5(decoderinstruct_1_out_8), .in_6(dringcounter_1_t4), .out_7(c43_1_out_7),
    .out_8(c43_1_out_8), .out_9(nLo));

  // Notes on the sheet:
  //   CONTROL MATRIX
  //   C39
  //   C40
  //   C45
  //   C41
  //   C42
  //   C46
  //   C43
endmodule

module C39 (
  input  in_1,
  input  in_2,
  input  in_3,
  input  in_4,
  input  in_5,
  input  in_6,
  input  in_7,
  input  in_8,
  output out_9,
  output out_10,
  output out_11,
  output out_12
);

  nand nand_1 (out_9, in_1, in_2);
  nand nand_2 (out_10, in_3, in_4);
  nand nand_3 (out_11, in_5, in_6);
  nand nand_4 (out_12, in_7, in_8);
endmodule

module C43 (
  input  in_1,
  input  in_2,
  input  in_3,
  input  in_4,
  input  in_5,
  input  in_6,
  output out_7,
  output out_8,
  output out_9
);

  nand nand_1 (out_7, in_1, in_2);
  nand nand_2 (out_8, in_3, in_4);
  nand nand_3 (out_9, in_5, in_6);
endmodule

module SAP_ARC (
  input  in_1,
  input  in_2,
  input  in_3,
  input  in_4,
  input  in_5
);

  wire ir_register_1_out_13, ir_register_1_out_14, ir_register_1_out_15, ir_register_1_out_16,
       ir_register_1_out_17, ir_register_1_out_18, ir_register_1_out_19, ir_register_1_out_20, mar_1_a0_2,
       mar_1_a1_2, mar_1_a2_2, mar_1_a3_2, PC__1, PC__2, PC__3, PC__4, ram_1_out_16, ram_1_out_17,
       ram_1_out_18, ram_1_out_19, ram_1_out_20, ram_1_out_21, ram_1_out_22, ram_1_out_23, W_BUS_a1,
       W_BUS_a2, W_BUS_a3, W_BUS_a4, W_BUS_d1_2, W_BUS_d1_3, W_BUS_d2_2, W_BUS_d3_2, W_BUS_d4_2, W_BUS_d8,
       W_BUS_i1, W_BUS_i2, W_BUS_i3, W_BUS_i4, W_BUS_out_18, W_BUS_out_19, W_BUS_out_20, W_BUS_out_21,
       W_BUS_out_22, W_BUS_out_24, W_BUS_out_37, W_BUS_out_38, W_BUS_out_39, W_BUS_out_40, W_BUS_out_41,
       W_BUS_out_42, W_BUS_out_43, W_BUS_out_44;

  IR_REGISTER ir_register_1 (
    .in_1(W_BUS_i4), .in_2(W_BUS_i3), .in_3(W_BUS_i2), .in_4(W_BUS_d4_2), .in_5(W_BUS_d3_2),
    .in_6(W_BUS_d2_2), .in_7(W_BUS_d1_3), .in_8(W_BUS_i1), .out_13(ir_register_1_out_13),
    .out_14(ir_register_1_out_14), .out_15(ir_register_1_out_15), .out_16(ir_register_1_out_16),
    .out_17(ir_register_1_out_17), .out_18(ir_register_1_out_18), .out_19(ir_register_1_out_19),
    .out_20(ir_register_1_out_20));  // open: CLR, nEi, in_9, in_12
  ProgramCounter PC (._4(PC__4), ._3(PC__3), ._2(PC__2), ._1(PC__1));  // open: Cp, nCLK, nCLR, Ep
  MAR mar_1 (
    .A0(in_1), .A1(in_2), .A2(in_3), .A3(in_4), .PROG(in_5), .in_1(W_BUS_a4), .in_2(W_BUS_a3),
    .in_3(W_BUS_a2), .in_4(W_BUS_a1), .A3_2(mar_1_a3_2), .A2_2(mar_1_a2_2), .A1_2(mar_1_a1_2),
    .A0_2(mar_1_a0_2));  // open: in_5, in_6
  ControlMatrix controlmatrix_1 (
    .I4(ir_register_1_out_13), .I3(ir_register_1_out_14), .I2(ir_register_1_out_15), .I1(ir_register_1_out_16));  // open: in_1, in_2, out_7, Cp, Ep, nLm, nCe, nLi, nEi, nLa, Ea, Su, Eu, nLb, nLo
  RAM ram_1 (
    .out_16(ram_1_out_16), .out_17(ram_1_out_17), .out_18(ram_1_out_18), .out_19(ram_1_out_19),
    .in_1(mar_1_a3_2), .in_2(mar_1_a2_2), .in_3(mar_1_a1_2), .in_4(mar_1_a0_2), .out_20(ram_1_out_20),
    .out_21(ram_1_out_21), .out_22(ram_1_out_22), .out_23(ram_1_out_23));  // open: in_13, in_14, in_5, in_6, in_7, in_8, in_9, in_10, in_11, in_12, nCE
  W_BUS W_BUS (
    .PC1(PC__1), .PC2(PC__2), .PC3(PC__3), .PC4(PC__4), .A4(W_BUS_a4), .A3(W_BUS_a3), .A2(W_BUS_a2),
    .A1(W_BUS_a1), .D4_2(W_BUS_d4_2), .D3_2(W_BUS_d3_2), .D2_2(W_BUS_d2_2), .D1_3(W_BUS_d1_3),
    .Mo8(ram_1_out_17), .in_11(ram_1_out_18), .in_10(ram_1_out_19), .in_9(ram_1_out_23), .in_8(ram_1_out_22),
    .in_7(ram_1_out_21), .in_6(ram_1_out_20), .Mo1(ram_1_out_16), .I4(W_BUS_i4), .I3(W_BUS_i3),
    .I2(W_BUS_i2), .I1(W_BUS_i1), .out_37(W_BUS_out_37), .out_38(W_BUS_out_38), .out_39(W_BUS_out_39),
    .out_40(W_BUS_out_40), .out_41(W_BUS_out_41), .out_42(W_BUS_out_42), .out_43(W_BUS_out_43),
    .out_44(W_BUS_out_44), .D1(ir_register_1_out_20), .D2(ir_register_1_out_19), .D3(ir_register_1_out_18),
    .D4(ir_register_1_out_17), .D1_2(W_BUS_d1_2), .out_18(W_BUS_out_18), .out_19(W_BUS_out_19),
    .out_20(W_BUS_out_20), .out_21(W_BUS_out_21), .out_22(W_BUS_out_22), .D8(W_BUS_d8), .out_24(W_BUS_out_24));
  LED led_1 (.in(W_BUS_out_38));
  LED led_2 (.in(W_BUS_out_37));
  LED led_3 (.in(W_BUS_out_39));
  LED led_4 (.in(W_BUS_out_43));
  LED led_5 (.in(W_BUS_out_42));
  LED led_6 (.in(W_BUS_out_41));
  LED led_7 (.in(W_BUS_out_40));
  ULA ula_1 ();  // open: B4, B3, B2, B1, B5, B6, B7, B8, Su, A1, A2, A3, A4, A8, A7, A6, A5, out_23, out_24, out_25, out_26, out_19, out_20, out_21, out_22, Eu
  LED led_8 (.in(W_BUS_out_44));
  Acommulator acommulator_1 (
    .D8(W_BUS_out_24), .D7(W_BUS_d8), .D6(W_BUS_out_22), .D5(W_BUS_out_21), .D4(W_BUS_out_20),
    .D3(W_BUS_out_19), .D2(W_BUS_out_18), .D1(W_BUS_d1_2));  // open: O1, O2, O3, O4, O5, O6, O7, O8, nLm, CLK, Ea, _8, _7, _6, _5, _4, _3, _2, _1
  B_Register b_register_1 ();  // open: nLb, CLK, D8, D7, D6, D5, D4, D3, D2, D1, _8, _7, _6, _5, _4, _3, _2, _1

  // Notes on the sheet:
  //   MAR
  //   CONTROL MTX
  //   IR
endmodule

module ProgramCounter (
  input  Cp,
  input  nCLK,
  input  nCLR,
  input  Ep,
  output _4,
  output _3,
  output _2,
  output _1
);

  wire j_k_ff_1_q, j_k_ff_2_q, j_k_ff_3_q, j_k_ff_4_q, not_1_out, not_2_out, not_3_out, not_4_out, not_5_out,
       not_6_out, not_7_out, not_8_out;

  J_K_Flip_Flop j_k_ff_1 (.J(Cp), .clk(not_1_out), .K(Cp), .Q(j_k_ff_1_q), .reset(not_2_out));  // open: Qn, preset, en
  not not_1 (not_1_out, nCLK);
  not not_2 (not_2_out, nCLR);
  not not_3 (not_3_out, j_k_ff_1_q);
  assign _1 = Ep ? j_k_ff_1_q : 1'bz;  // Controlled_Buffer controlled_buffer_1
  J_K_Flip_Flop j_k_ff_2 (.J(Cp), .clk(not_3_out), .K(Cp), .Q(j_k_ff_2_q), .reset(not_5_out));  // open: Qn, preset, en
  not not_4 (not_4_out, j_k_ff_2_q);
  not not_5 (not_5_out, nCLR);
  assign _2 = Ep ? j_k_ff_2_q : 1'bz;  // Controlled_Buffer controlled_buffer_2
  J_K_Flip_Flop j_k_ff_3 (.J(Cp), .clk(not_4_out), .K(Cp), .Q(j_k_ff_3_q), .reset(not_6_out));  // open: Qn, preset, en
  not not_6 (not_6_out, nCLR);
  assign _3 = Ep ? j_k_ff_3_q : 1'bz;  // Controlled_Buffer controlled_buffer_3
  not not_7 (not_7_out, j_k_ff_3_q);
  not not_8 (not_8_out, nCLR);
  J_K_Flip_Flop j_k_ff_4 (.J(Cp), .clk(not_7_out), .K(Cp), .Q(j_k_ff_4_q), .reset(not_8_out));  // open: Qn, preset, en
  assign _4 = Ep ? j_k_ff_4_q : 1'bz;  // Controlled_Buffer controlled_buffer_4
endmodule

module C44 (
  input  in_1,
  input  in_2,
  input  in_3,
  input  in_4,
  input  in_5,
  input  in_6,
  input  in_7,
  input  in_8,
  output out_9,
  output out_10
);

  wire not_1_out, not_2_out, not_3_out, not_4_out, not_5_out, not_6_out, not_7_out, not_8_out;

  not not_1 (not_1_out, in_2);
  not not_2 (not_2_out, in_1);
  not not_3 (not_3_out, in_3);
  nor nor_1 (out_9, not_2_out, not_1_out, not_3_out, not_4_out);
  not not_4 (not_4_out, in_4);
  not not_5 (not_5_out, in_5);
  not not_6 (not_6_out, in_8);
  not not_7 (not_7_out, in_7);
  not not_8 (not_8_out, in_6);
  nor nor_2 (out_10, not_5_out, not_8_out, not_7_out, not_6_out);
endmodule

module C45 (
  input  in_1,
  input  in_2,
  input  in_3,
  input  in_4,
  input  in_5,
  input  in_6,
  output out_7,
  output out_8
);

  wire not_1_out, not_2_out, not_3_out, not_4_out, not_5_out, not_6_out;

  not not_1 (not_1_out, in_2);
  not not_2 (not_2_out, in_1);
  nor nor_1 (out_7, not_2_out, not_1_out, not_3_out);
  not not_3 (not_3_out, in_3);
  not not_4 (not_4_out, in_4);
  not not_5 (not_5_out, in_5);
  nor nor_2 (out_8, not_4_out, not_5_out, not_6_out);
  not not_6 (not_6_out, in_6);
endmodule

module C46 (
  input  in_1,
  input  in_2,
  input  in_3,
  input  in_4,
  output out_5,
  output out_6
);

  wire not_1_out, not_2_out, not_3_out, not_4_out;

  not not_1 (not_1_out, in_1);
  or or_1 (out_5, not_1_out, not_2_out);
  not not_2 (not_2_out, in_2);
  not not_3 (not_3_out, in_4);
  not not_4 (not_4_out, in_3);
  or or_2 (out_6, not_4_out, not_3_out);
endmodule

module BufferRegister (
  input  X0,
  input  X1,
  input  X2,
  input  X3,
  input  LOAD,
  input  CLK,
  input  CLR,
  input  ENABLE,
  output D0,
  output D1,
  output D2,
  output D3
);

  wire and_1_out, and_2_out, and_3_out, and_4_out, and_5_out, and_6_out, and_7_out, and_8_out, d_ff_1_q,
       d_ff_2_q, d_ff_3_q, d_ff_4_q, not_1_out, or_1_out, or_2_out, or_3_out, or_4_out;

  not not_1 (not_1_out, LOAD);
  and and_1 (and_1_out, LOAD, X0);
  and and_2 (and_2_out, not_1_out, d_ff_1_q);
  or or_1 (or_1_out, and_1_out, and_2_out);
  and and_3 (and_3_out, LOAD, X1);
  or or_2 (or_2_out, and_3_out, and_5_out);
  D_Flip_Flop d_ff_1 (.clk(CLK), .D(or_1_out), .Q(d_ff_1_q), .reset(CLR));  // open: Qn, preset, en
  assign D0 = ENABLE ? d_ff_1_q : 1'bz;  // Controlled_Buffer controlled_buffer_1
  and and_4 (and_4_out, LOAD, X2);
  and and_5 (and_5_out, not_1_out, d_ff_2_q);
  D_Flip_Flop d_ff_2 (.clk(CLK), .D(or_2_out), .Q(d_ff_2_q), .reset(CLR));  // open: Qn, preset, en
  assign D1 = ENABLE ? d_ff_2_q : 1'bz;  // Controlled_Buffer controlled_buffer_2
  and and_6 (and_6_out, not_1_out, d_ff_3_q);
  or or_3 (or_3_out, and_4_out, and_6_out);
  D_Flip_Flop d_ff_3 (.clk(CLK), .D(or_3_out), .Q(d_ff_3_q), .reset(CLR));  // open: Qn, preset, en
  assign D2 = ENABLE ? d_ff_3_q : 1'bz;  // Controlled_Buffer controlled_buffer_3
  and and_7 (and_7_out, LOAD, X3);
  and and_8 (and_8_out, not_1_out, d_ff_4_q);
  or or_4 (or_4_out, and_7_out, and_8_out);
  D_Flip_Flop d_ff_4 (.clk(CLK), .D(or_4_out), .Q(d_ff_4_q), .reset(CLR));  // open: Qn, preset, en
  assign D3 = ENABLE ? d_ff_4_q : 1'bz;  // Controlled_Buffer controlled_buffer_4
endmodule

module MAR (
  input  in_1,
  input  in_2,
  input  in_3,
  input  in_4,
  input  in_5,
  input  in_6,
  input  A0,
  input  A1,
  input  A2,
  input  A3,
  input  PROG,
  output A3_2,
  output A2_2,
  output A1_2,
  output A0_2
);

  wire bufferregister_1_d0, bufferregister_1_d1, bufferregister_1_d2, bufferregister_1_d3,
       n2to1multiplexer_1_out_10, n2to1multiplexer_1_out_11, n2to1multiplexer_1_out_12,
       n2to1multiplexer_1_out_13, not_1_out;

  BufferRegister bufferregister_1 (
    .LOAD(in_5), .CLK(in_6), .CLR(not_1_out), .ENABLE(1'b1), .X0(in_4), .X1(in_3), .X2(in_2), .X3(in_1),
    .D0(bufferregister_1_d0), .D1(bufferregister_1_d1), .D2(bufferregister_1_d2), .D3(bufferregister_1_d3));
  not not_1 (not_1_out, 1'b1);
  _2TO1MULTIPLEXER u_2to1multiplexer_1 (
    .in_9(PROG), .in_1(A3), .in_2(bufferregister_1_d3), .in_3(A2), .in_4(bufferregister_1_d2), .in_5(A1),
    .in_6(bufferregister_1_d1), .in_7(A0), .in_8(bufferregister_1_d0), .out_10(n2to1multiplexer_1_out_10),
    .out_11(n2to1multiplexer_1_out_11), .out_12(n2to1multiplexer_1_out_12), .out_13(n2to1multiplexer_1_out_13));
  not not_2 (A2_2, n2to1multiplexer_1_out_11);
  not not_3 (A3_2, n2to1multiplexer_1_out_10);
  not not_4 (A1_2, n2to1multiplexer_1_out_12);
  not not_5 (A0_2, n2to1multiplexer_1_out_13);
endmodule

module _2TO1MULTIPLEXER (
  input  in_1,
  input  in_2,
  input  in_3,
  input  in_4,
  input  in_5,
  input  in_6,
  input  in_7,
  input  in_8,
  input  in_9,
  output out_10,
  output out_11,
  output out_12,
  output out_13
);

  wire and_1_out, and_2_out, and_3_out, and_4_out, and_5_out, and_6_out, and_7_out, and_8_out, and_9_out,
       and_10_out, not_1_out, not_2_out, not_3_out, not_4_out, not_5_out;

  not not_1 (not_1_out, in_9);
  not not_2 (not_2_out, not_1_out);
  and and_1 (and_1_out, not_2_out, not_5_out);
  not not_3 (not_3_out, in_9);
  not not_4 (not_4_out, 1'b0);
  not not_5 (not_5_out, 1'b0);
  and and_2 (and_2_out, not_3_out, not_4_out);
  and and_3 (and_3_out, and_1_out, in_1);
  nor nor_1 (out_10, and_3_out, and_4_out);
  and and_4 (and_4_out, and_2_out, in_2);
  and and_5 (and_5_out, and_1_out, in_3);
  and and_6 (and_6_out, and_2_out, in_4);
  nor nor_2 (out_11, and_5_out, and_6_out);
  and and_7 (and_7_out, and_1_out, in_5);
  nor nor_3 (out_12, and_7_out, and_8_out);
  and and_8 (and_8_out, and_2_out, in_6);
  and and_9 (and_9_out, and_1_out, in_7);
  and and_10 (and_10_out, and_2_out, in_8);
  nor nor_4 (out_13, and_9_out, and_10_out);
endmodule

module IR_REGISTER (
  input  in_1,
  input  in_2,
  input  in_3,
  input  in_4,
  input  in_5,
  input  in_6,
  input  in_7,
  input  in_8,
  input  in_9,
  input  CLR,
  input  nEi,
  input  in_12,
  output out_13,
  output out_14,
  output out_15,
  output out_16,
  output out_17,
  output out_18,
  output out_19,
  output out_20
);

  wire not_1_out;

  BufferRegister bufferregister_1 (
    .LOAD(in_9), .CLK(in_12), .CLR(CLR), .ENABLE(1'b1), .X0(in_4), .X1(in_3), .X2(in_2), .X3(in_1),
    .D0(out_16), .D1(out_15), .D2(out_14), .D3(out_13));
  BufferRegister bufferregister_2 (
    .LOAD(in_9), .CLK(in_12), .CLR(1'b0), .ENABLE(not_1_out), .X0(in_8), .X1(in_7), .X2(in_6), .X3(in_5),
    .D0(out_20), .D1(out_19), .D2(out_18), .D3(out_17));
  not not_1 (not_1_out, nEi);
endmodule

module W_BUS (
  input  PC1,
  input  PC2,
  input  PC3,
  input  PC4,
  input  Mo1,
  input  in_6,
  input  in_7,
  input  in_8,
  input  in_9,
  input  in_10,
  input  in_11,
  input  Mo8,
  input  D1,
  input  D2,
  input  D3,
  input  D4,
  output D1_2,
  output out_18,
  output out_19,
  output out_20,
  output out_21,
  output out_22,
  output D8,
  output out_24,
  output A4,
  output A3,
  output A2,
  output A1,
  output I4,
  output I3,
  output I2,
  output I1,
  output D4_2,
  output D3_2,
  output D2_2,
  output D1_3,
  output out_37,
  output out_38,
  output out_39,
  output out_40,
  output out_41,
  output out_42,
  output out_43,
  output out_44
);


  assign A1 = D1;
  assign A2 = D2;
  assign A3 = D3;
  assign A4 = D4;
  assign D1_2 = D1;
  assign D1_3 = D1;
  assign D2_2 = D2;
  assign D3_2 = D3;
  assign D4_2 = D4;
  assign D8 = in_11;
  assign I1 = in_9;
  assign I2 = in_10;
  assign I3 = in_11;
  assign I4 = Mo8;
  assign in_6 = D2;
  assign in_7 = D3;
  assign in_8 = D4;
  assign Mo1 = D1;
  assign out_18 = D2;
  assign out_19 = D3;
  assign out_20 = D4;
  assign out_21 = in_9;
  assign out_22 = in_10;
  assign out_24 = Mo8;
  assign out_37 = Mo8;
  assign out_38 = in_11;
  assign out_39 = in_10;
  assign out_40 = in_9;
  assign out_41 = D4;
  assign out_42 = D3;
  assign out_43 = D2;
  assign out_44 = D1;
  assign PC1 = D1;
  assign PC2 = D2;
  assign PC3 = D3;
  assign PC4 = D4;

  // Notes on the sheet:
  //   PC DATA
endmodule

module RAM_MEMORY (
  input  in_1,
  input  in_2,
  input  in_3,
  input  in_4,
  input  in_5,
  input  in_6,
  input  in_7,
  input  in_8,
  input  in_9,
  input  in_10,
  output Do4,
  output Do3,
  output Do2,
  output Do1
);

  wire and_1_out, and_2_out, and_3_out, and_4_out, and_5_out, and_6_out, and_7_out, and_8_out, and_9_out,
       and_10_out, and_11_out, and_12_out, and_13_out, and_14_out, and_15_out, and_16_out, not_1_out,
       not_2_out, not_3_out, not_4_out, ram4bitschunk_1_output, ram4bitschunk_1_output_2,
       ram4bitschunk_1_output_3, ram4bitschunk_1_output_4, ram4bitschunk_2_output, ram4bitschunk_2_output_2,
       ram4bitschunk_2_output_3, ram4bitschunk_2_output_4, ram4bitschunk_3_output, ram4bitschunk_3_output_2,
       ram4bitschunk_3_output_3, ram4bitschunk_3_output_4, ram4bitschunk_4_output, ram4bitschunk_4_output_2,
       ram4bitschunk_4_output_3, ram4bitschunk_4_output_4, ram4bitschunk_5_output, ram4bitschunk_5_output_2,
       ram4bitschunk_5_output_3, ram4bitschunk_5_output_4, ram4bitschunk_6_output, ram4bitschunk_6_output_2,
       ram4bitschunk_6_output_3, ram4bitschunk_6_output_4, ram4bitschunk_7_output, ram4bitschunk_7_output_2,
       ram4bitschunk_7_output_3, ram4bitschunk_7_output_4, ram4bitschunk_8_output, ram4bitschunk_8_output_2,
       ram4bitschunk_8_output_3, ram4bitschunk_8_output_4, ram4bitschunk_9_output, ram4bitschunk_9_output_2,
       ram4bitschunk_9_output_3, ram4bitschunk_9_output_4, ram4bitschunk_10_output,
       ram4bitschunk_10_output_2, ram4bitschunk_10_output_3, ram4bitschunk_10_output_4,
       ram4bitschunk_11_output, ram4bitschunk_11_output_2, ram4bitschunk_11_output_3,
       ram4bitschunk_11_output_4, ram4bitschunk_12_output, ram4bitschunk_12_output_2,
       ram4bitschunk_12_output_3, ram4bitschunk_12_output_4, ram4bitschunk_13_output,
       ram4bitschunk_13_output_2, ram4bitschunk_13_output_3, ram4bitschunk_13_output_4,
       ram4bitschunk_14_output, ram4bitschunk_14_output_2, ram4bitschunk_14_output_3,
       ram4bitschunk_14_output_4, ram4bitschunk_15_output, ram4bitschunk_15_output_2,
       ram4bitschunk_15_output_3, ram4bitschunk_15_output_4, ram4bitschunk_16_output,
       ram4bitschunk_16_output_2, ram4bitschunk_16_output_3, ram4bitschunk_16_output_4;

  not not_1 (not_1_out, in_1);
  not not_2 (not_2_out, in_2);
  not not_3 (not_3_out, in_3);
  not not_4 (not_4_out, in_4);
  and and_1 (and_1_out, not_4_out, not_3_out, not_2_out, not_1_out);
  and and_2 (and_2_out, in_4, not_3_out, not_2_out, not_1_out);
  and and_3 (and_3_out, in_3, not_4_out, not_2_out, not_1_out);
  and and_4 (and_4_out, in_4, in_3, not_2_out, not_1_out);
  and and_5 (and_5_out, not_4_out, not_3_out, in_2, not_1_out);
  and and_6 (and_6_out, in_4, not_3_out, in_2, not_1_out);
  and and_7 (and_7_out, not_4_out, in_3, in_2, not_1_out);
  and and_8 (and_8_out, in_4, in_3, in_2, not_1_out);
  and and_9 (and_9_out, not_4_out, not_3_out, not_2_out, in_1);
  and and_10 (and_10_out, in_4, not_3_out, not_2_out, in_1);
  and and_11 (and_11_out, not_4_out, in_3, not_2_out, in_1);
  and and_12 (and_12_out, in_4, in_3, not_2_out, in_1);
  and and_13 (and_13_out, not_4_out, not_3_out, in_2, in_1);
  and and_14 (and_14_out, in_4, not_3_out, in_2, in_1);
  and and_15 (and_15_out, not_4_out, in_3, in_2, in_1);
  and and_16 (and_16_out, in_4, in_3, in_2, in_1);
  Ram4bitsChunk ram4bitschunk_1 (
    .in_1(and_15_out), .clk(in_10), .\input (in_8), .input_2(in_7), .input_3(in_6), .input_4(in_9),
    .\output (ram4bitschunk_1_output), .output_2(ram4bitschunk_1_output_2),
    .output_3(ram4bitschunk_1_output_3), .output_4(ram4bitschunk_1_output_4), .read_write(in_5));
  Ram4bitsChunk ram4bitschunk_2 (
    .in_1(and_16_out), .clk(in_10), .\input (in_8), .input_2(in_7), .input_3(in_6), .input_4(in_9),
    .\output (ram4bitschunk_2_output), .output_2(ram4bitschunk_2_output_2),
    .output_3(ram4bitschunk_2_output_3), .output_4(ram4bitschunk_2_output_4), .read_write(in_5));
  Ram4bitsChunk ram4bitschunk_3 (
    .in_1(and_1_out), .clk(in_10), .\input (in_8), .input_2(in_7), .input_3(in_6), .input_4(in_9),
    .\output (ram4bitschunk_3_output), .output_2(ram4bitschunk_3_output_2),
    .output_3(ram4bitschunk_3_output_3), .output_4(ram4bitschunk_3_output_4), .read_write(in_5));
  Ram4bitsChunk ram4bitschunk_4 (
    .in_1(and_2_out), .clk(in_10), .\input (in_8), .input_2(in_7), .input_3(in_6), .input_4(in_9),
    .\output (ram4bitschunk_4_output), .output_2(ram4bitschunk_4_output_2),
    .output_3(ram4bitschunk_4_output_3), .output_4(ram4bitschunk_4_output_4), .read_write(in_5));
  Ram4bitsChunk ram4bitschunk_5 (
    .in_1(and_3_out), .clk(in_10), .\input (in_8), .input_2(in_7), .input_3(in_6), .input_4(in_9),
    .\output (ram4bitschunk_5_output), .output_2(ram4bitschunk_5_output_2),
    .output_3(ram4bitschunk_5_output_3), .output_4(ram4bitschunk_5_output_4), .read_write(in_5));
  Ram4bitsChunk ram4bitschunk_6 (
    .in_1(and_4_out), .clk(in_10), .\input (in_8), .input_2(in_7), .input_3(in_6), .input_4(in_9),
    .\output (ram4bitschunk_6_output), .output_2(ram4bitschunk_6_output_2),
    .output_3(ram4bitschunk_6_output_3), .output_4(ram4bitschunk_6_output_4), .read_write(in_5));
  Ram4bitsChunk ram4bitschunk_7 (
    .in_1(and_5_out), .clk(in_10), .\input (in_8), .input_2(in_7), .input_3(in_6), .input_4(in_9),
    .\output (ram4bitschunk_7_output), .output_2(ram4bitschunk_7_output_2),
    .output_3(ram4bitschunk_7_output_3), .output_4(ram4bitschunk_7_output_4), .read_write(in_5));
  Ram4bitsChunk ram4bitschunk_8 (
    .in_1(and_6_out), .clk(in_10), .\input (in_8), .input_2(in_7), .input_3(in_6), .input_4(in_9),
    .\output (ram4bitschunk_8_output), .output_2(ram4bitschunk_8_output_2),
    .output_3(ram4bitschunk_8_output_3), .output_4(ram4bitschunk_8_output_4), .read_write(in_5));
  Ram4bitsChunk ram4bitschunk_9 (
    .in_1(and_7_out), .clk(in_10), .\input (in_8), .input_2(in_7), .input_3(in_6), .input_4(in_9),
    .\output (ram4bitschunk_9_output), .output_2(ram4bitschunk_9_output_2),
    .output_3(ram4bitschunk_9_output_3), .output_4(ram4bitschunk_9_output_4), .read_write(in_5));
  Ram4bitsChunk ram4bitschunk_10 (
    .in_1(and_8_out), .clk(in_10), .\input (in_8), .input_2(in_7), .input_3(in_6), .input_4(in_9),
    .\output (ram4bitschunk_10_output), .output_2(ram4bitschunk_10_output_2),
    .output_3(ram4bitschunk_10_output_3), .output_4(ram4bitschunk_10_output_4), .read_write(in_5));
  Ram4bitsChunk ram4bitschunk_11 (
    .in_1(and_9_out), .clk(in_10), .\input (in_8), .input_2(in_7), .input_3(in_6), .input_4(in_9),
    .\output (ram4bitschunk_11_output), .output_2(ram4bitschunk_11_output_2),
    .output_3(ram4bitschunk_11_output_3), .output_4(ram4bitschunk_11_output_4), .read_write(in_5));
  Ram4bitsChunk ram4bitschunk_12 (
    .in_1(and_10_out), .clk(in_10), .\input (in_8), .input_2(in_7), .input_3(in_6), .input_4(in_9),
    .\output (ram4bitschunk_12_output), .output_2(ram4bitschunk_12_output_2),
    .output_3(ram4bitschunk_12_output_3), .output_4(ram4bitschunk_12_output_4), .read_write(in_5));
  Ram4bitsChunk ram4bitschunk_13 (
    .in_1(and_11_out), .clk(in_10), .\input (in_8), .input_2(in_7), .input_3(in_6), .input_4(in_9),
    .\output (ram4bitschunk_13_output), .output_2(ram4bitschunk_13_output_2),
    .output_3(ram4bitschunk_13_output_3), .output_4(ram4bitschunk_13_output_4), .read_write(in_5));
  Ram4bitsChunk ram4bitschunk_14 (
    .in_1(and_12_out), .clk(in_10), .\input (in_8), .input_2(in_7), .input_3(in_6), .input_4(in_9),
    .\output (ram4bitschunk_14_output), .output_2(ram4bitschunk_14_output_2),
    .output_3(ram4bitschunk_14_output_3), .output_4(ram4bitschunk_14_output_4), .read_write(in_5));
  Ram4bitsChunk ram4bitschunk_15 (
    .in_1(and_13_out), .clk(in_10), .\input (in_8), .input_2(in_7), .input_3(in_6), .input_4(in_9),
    .\output (ram4bitschunk_15_output), .output_2(ram4bitschunk_15_output_2),
    .output_3(ram4bitschunk_15_output_3), .output_4(ram4bitschunk_15_output_4), .read_write(in_5));
  Ram4bitsChunk ram4bitschunk_16 (
    .in_1(and_14_out), .clk(in_10), .\input (in_8), .input_2(in_7), .input_3(in_6), .input_4(in_9),
    .\output (ram4bitschunk_16_output), .output_2(ram4bitschunk_16_output_2),
    .output_3(ram4bitschunk_16_output_3), .output_4(ram4bitschunk_16_output_4), .read_write(in_5));
  or or_1 (Do4, ram4bitschunk_2_output_3, ram4bitschunk_1_output_3, ram4bitschunk_16_output_3, ram4bitschunk_15_output_3, ram4bitschunk_14_output_3, ram4bitschunk_13_output_3, ram4bitschunk_12_output_3, ram4bitschunk_11_output_3, ram4bitschunk_10_output_3, ram4bitschunk_9_output_3, ram4bitschunk_8_output_3, ram4bitschunk_7_output_3, ram4bitschunk_6_output_3, ram4bitschunk_5_output_3, ram4bitschunk_4_output_3, ram4bitschunk_3_output_3);
  or or_2 (Do3, ram4bitschunk_2_output_2, ram4bitschunk_1_output_2, ram4bitschunk_16_output_2, ram4bitschunk_15_output_2, ram4bitschunk_14_output_2, ram4bitschunk_13_output_2, ram4bitschunk_12_output_2, ram4bitschunk_11_output_2, ram4bitschunk_10_output_2, ram4bitschunk_9_output_2, ram4bitschunk_8_output_2, ram4bitschunk_7_output_2, ram4bitschunk_6_output_2, ram4bitschunk_5_output_2, ram4bitschunk_4_output_2, ram4bitschunk_3_output_2);
  or or_3 (Do2, ram4bitschunk_2_output, ram4bitschunk_1_output, ram4bitschunk_16_output, ram4bitschunk_15_output, ram4bitschunk_14_output, ram4bitschunk_13_output, ram4bitschunk_12_output, ram4bitschunk_11_output, ram4bitschunk_10_output, ram4bitschunk_9_output, ram4bitschunk_8_output, ram4bitschunk_7_output, ram4bitschunk_6_output, ram4bitschunk_5_output, ram4bitschunk_4_output, ram4bitschunk_3_output);
  or or_4 (Do1, ram4bitschunk_2_output_4, ram4bitschunk_1_output_4, ram4bitschunk_16_output_4, ram4bitschunk_15_output_4, ram4bitschunk_14_output_4, ram4bitschunk_13_output_4, ram4bitschunk_12_output_4, ram4bitschunk_11_output_4, ram4bitschunk_10_output_4, ram4bitschunk_9_output_4, ram4bitschunk_8_output_4, ram4bitschunk_7_output_4, ram4bitschunk_6_output_4, ram4bitschunk_5_output_4, ram4bitschunk_4_output_4, ram4bitschunk_3_output_4);
endmodule

module Ram4bitsChunk (
  input  in_1,
  input  clk,
  input  \input ,
  input  input_2,
  input  input_3,
  input  input_4,
  input  read_write,
  output \output ,
  output output_2,
  output output_3,
  output output_4
);

  wire and_1_out, and_2_out, and_4_out, and_5_out, and_7_out, and_8_out, and_10_out, and_11_out, not_1_out,
       not_2_out, not_3_out, not_4_out, not_5_out, not_6_out, not_7_out, not_8_out, s_r_ff_1_q, s_r_ff_1_qn,
       s_r_ff_2_q, s_r_ff_2_qn, s_r_ff_3_q, s_r_ff_3_qn, s_r_ff_4_q, s_r_ff_4_qn;

  not not_1 (not_1_out, input_4);
  and and_1 (and_1_out, in_1, input_4, read_write);
  and and_2 (and_2_out, in_1, not_1_out, read_write);
  S_R_Flip_Flop s_r_ff_1 (
    .S(and_1_out), .clk(clk), .R(and_2_out), .Q(s_r_ff_1_q), .Qn(s_r_ff_1_qn), .preset(1'b0), .reset(1'b0),
    .en(1'b1));
  not not_2 (not_2_out, read_write);
  and and_3 (output_4, in_1, s_r_ff_1_q, not_2_out);
  not not_3 (not_3_out, \input );
  and and_4 (and_4_out, in_1, \input , read_write);
  and and_5 (and_5_out, in_1, not_3_out, read_write);
  S_R_Flip_Flop s_r_ff_2 (
    .S(and_4_out), .clk(clk), .R(and_5_out), .Q(s_r_ff_2_q), .Qn(s_r_ff_2_qn), .preset(1'b0), .reset(1'b0),
    .en(1'b1));
  not not_4 (not_4_out, read_write);
  and and_6 (\output , in_1, s_r_ff_2_q, not_4_out);
  not not_5 (not_5_out, input_2);
  and and_7 (and_7_out, in_1, input_2, read_write);
  and and_8 (and_8_out, in_1, not_5_out, read_write);
  S_R_Flip_Flop s_r_ff_3 (
    .S(and_7_out), .clk(clk), .R(and_8_out), .Q(s_r_ff_3_q), .Qn(s_r_ff_3_qn), .preset(1'b0), .reset(1'b0),
    .en(1'b1));
  not not_6 (not_6_out, read_write);
  and and_9 (output_2, in_1, s_r_ff_3_q, not_6_out);
  not not_7 (not_7_out, input_3);
  and and_10 (and_10_out, in_1, input_3, read_write);
  and and_11 (and_11_out, in_1, not_7_out, read_write);
  S_R_Flip_Flop s_r_ff_4 (
    .S(and_10_out), .clk(clk), .R(and_11_out), .Q(s_r_ff_4_q), .Qn(s_r_ff_4_qn), .preset(1'b0), .reset(1'b0),
    .en(1'b1));
  not not_8 (not_8_out, read_write);
  and and_12 (output_3, in_1, s_r_ff_4_q, not_8_out);
  // also tied to GND on the sheet: {s_r_ff_1_qn, s_r_ff_2_qn, s_r_ff_3_qn, s_r_ff_4_qn}

  // Notes on the sheet:
  //   clk
  //   select
  //   select
  //   read/write
  //   select
  //   read/write
  //   select
  //   read/write
endmodule

module RAM (
  input  in_1,
  input  in_2,
  input  in_3,
  input  in_4,
  input  in_5,
  input  in_6,
  input  in_7,
  input  in_8,
  input  in_9,
  input  in_10,
  input  in_11,
  input  in_12,
  input  in_13,
  input  in_14,
  input  nCE,
  output out_16,
  output out_17,
  output out_18,
  output out_19,
  output out_20,
  output out_21,
  output out_22,
  output out_23
);

  wire ram_memory_1_do1, ram_memory_1_do2, ram_memory_1_do3, ram_memory_1_do4, ram_memory_2_do1,
       ram_memory_2_do2, ram_memory_2_do3, ram_memory_2_do4;

  // Buffer buffer_1 is placed but not wired
  RAM_MEMORY ram_memory_1 (
    .in_10(in_14), .in_1(in_1), .in_2(in_2), .in_3(in_3), .in_4(in_4), .in_6(in_5), .in_7(in_6), .in_8(in_7),
    .in_9(in_8), .in_5(in_13), .Do4(ram_memory_1_do4), .Do3(ram_memory_1_do3), .Do2(ram_memory_1_do2),
    .Do1(ram_memory_1_do1));
  assign out_20 = nCE ? ram_memory_1_do4 : 1'bz;  // Controlled_Buffer controlled_buffer_1
  assign out_22 = nCE ? ram_memory_1_do2 : 1'bz;  // Controlled_Buffer controlled_buffer_2
  assign out_21 = nCE ? ram_memory_1_do3 : 1'bz;  // Controlled_Buffer controlled_buffer_3
  assign out_23 = nCE ? ram_memory_1_do1 : 1'bz;  // Controlled_Buffer controlled_buffer_4
  RAM_MEMORY ram_memory_2 (
    .in_10(in_14), .in_1(in_1), .in_2(in_2), .in_3(in_3), .in_4(in_4), .in_6(in_9), .in_7(in_10),
    .in_8(in_11), .in_9(in_12), .in_5(in_13), .Do4(ram_memory_2_do4), .Do3(ram_memory_2_do3),
    .Do2(ram_memory_2_do2), .Do1(ram_memory_2_do1));
  assign out_16 = nCE ? ram_memory_2_do1 : 1'bz;  // Controlled_Buffer controlled_buffer_5
  assign out_17 = nCE ? ram_memory_2_do2 : 1'bz;  // Controlled_Buffer controlled_buffer_6
  assign out_18 = nCE ? ram_memory_2_do3 : 1'bz;  // Controlled_Buffer controlled_buffer_7
  assign out_19 = nCE ? ram_memory_2_do4 : 1'bz;  // Controlled_Buffer controlled_buffer_8
endmodule

module Acommulator (
  input  D8,
  input  D7,
  input  D6,
  input  D5,
  input  D4,
  input  D3,
  input  D2,
  input  D1,
  input  nLm,
  input  CLK,
  input  Ea,
  output O1,
  output O2,
  output O3,
  output O4,
  output O5,
  output O6,
  output O7,
  output O8,
  output _8,
  output _7,
  output _6,
  output _5,
  output _4,
  output _3,
  output _2,
  output _1
);

  assign O1 = Ea ? _1 : 1'bz;  // Controlled_Buffer controlled_buffer_1
  assign O2 = Ea ? _2 : 1'bz;  // Controlled_Buffer controlled_buffer_2
  assign O3 = Ea ? _3 : 1'bz;  // Controlled_Buffer controlled_buffer_3
  assign O4 = Ea ? _4 : 1'bz;  // Controlled_Buffer controlled_buffer_4
  assign O5 = Ea ? _5 : 1'bz;  // Controlled_Buffer controlled_buffer_5
  assign O6 = Ea ? _6 : 1'bz;  // Controlled_Buffer controlled_buffer_6
  assign O7 = Ea ? _7 : 1'bz;  // Controlled_Buffer controlled_buffer_7
  assign O8 = Ea ? _8 : 1'bz;  // Controlled_Buffer controlled_buffer_8
  BufferRegister bufferregister_1 (
    .LOAD(nLm), .CLK(CLK), .CLR(1'b0), .ENABLE(1'b1), .X0(D5), .X1(D6), .X2(D7), .X3(D8), .D0(_5), .D1(_6),
    .D2(_7), .D3(_8));
  BufferRegister bufferregister_2 (
    .LOAD(nLm), .CLK(CLK), .CLR(1'b0), .ENABLE(1'b1), .X0(D1), .X1(D2), .X2(D3), .X3(D4), .D0(_1), .D1(_2),
    .D2(_3), .D3(_4));
endmodule

module ULA (
  input  A8,
  input  A7,
  input  A6,
  input  A5,
  input  A4,
  input  A3,
  input  A2,
  input  A1,
  input  B8,
  input  B7,
  input  B6,
  input  B5,
  input  B4,
  input  B3,
  input  B2,
  input  B1,
  input  Su,
  input  Eu,
  output out_19,
  output out_20,
  output out_21,
  output out_22,
  output out_23,
  output out_24,
  output out_25,
  output out_26
);

  wire adder_subtractor_1_out_10, adder_subtractor_1_out_11, adder_subtractor_1_out_12,
       adder_subtractor_1_out_13, adder_subtractor_1_out_14, adder_subtractor_2_out_10,
       adder_subtractor_2_out_11, adder_subtractor_2_out_12, adder_subtractor_2_out_13,
       adder_subtractor_2_out_14, xor_1_out, xor_2_out, xor_3_out, xor_4_out, xor_5_out, xor_6_out,
       xor_7_out, xor_8_out;

  xor xor_1 (xor_1_out, B8, Su);
  Adder_subtractor adder_subtractor_1 (
    .in_9(adder_subtractor_2_out_14), .b4(xor_1_out), .a4(A8), .b3(xor_2_out), .a3(A7), .b2(xor_4_out),
    .a2(A6), .b1(xor_3_out), .a1(A5), .out_10(adder_subtractor_1_out_10), .out_11(adder_subtractor_1_out_11),
    .out_12(adder_subtractor_1_out_12), .out_13(adder_subtractor_1_out_13), .out_14(adder_subtractor_1_out_14));
  assign out_20 = Eu ? adder_subtractor_1_out_11 : 1'bz;  // Controlled_Buffer controlled_buffer_1
  assign out_19 = Eu ? adder_subtractor_1_out_10 : 1'bz;  // Controlled_Buffer controlled_buffer_2
  assign out_21 = Eu ? adder_subtractor_1_out_12 : 1'bz;  // Controlled_Buffer controlled_buffer_3
  assign out_22 = Eu ? adder_subtractor_1_out_13 : 1'bz;  // Controlled_Buffer controlled_buffer_4
  xor xor_2 (xor_2_out, B7, Su);
  xor xor_3 (xor_3_out, B5, Su);
  xor xor_4 (xor_4_out, B6, Su);
  Adder_subtractor adder_subtractor_2 (
    .in_9(Su), .b4(xor_5_out), .a4(A4), .b3(xor_7_out), .a3(A3), .b2(xor_6_out), .a2(A2), .b1(xor_8_out),
    .a1(A1), .out_10(adder_subtractor_2_out_10), .out_11(adder_subtractor_2_out_11),
    .out_12(adder_subtractor_2_out_12), .out_13(adder_subtractor_2_out_13), .out_14(adder_subtractor_2_out_14));
  assign out_26 = Eu ? adder_subtractor_2_out_13 : 1'bz;  // Controlled_Buffer controlled_buffer_5
  assign out_23 = Eu ? adder_subtractor_2_out_10 : 1'bz;  // Controlled_Buffer controlled_buffer_6
  assign out_24 = Eu ? adder_subtractor_2_out_11 : 1'bz;  // Controlled_Buffer controlled_buffer_7
  assign out_25 = Eu ? adder_subtractor_2_out_12 : 1'bz;  // Controlled_Buffer controlled_buffer_8
  xor xor_5 (xor_5_out, B4, Su);
  xor xor_6 (xor_6_out, B2, Su);
  xor xor_7 (xor_7_out, B3, Su);
  xor xor_8 (xor_8_out, B1, Su);
endmodule

module B_Register (
  input  D8,
  input  D7,
  input  D6,
  input  D5,
  input  D4,
  input  D3,
  input  D2,
  input  D1,
  input  nLb,
  input  CLK,
  output _8,
  output _7,
  output _6,
  output _5,
  output _4,
  output _3,
  output _2,
  output _1
);

  wire not_1_out, not_2_out;

  BufferRegister bufferregister_1 (
    .LOAD(not_1_out), .CLK(CLK), .CLR(1'b0), .ENABLE(1'b1), .X0(D5), .X1(D6), .X2(D7), .X3(D8), .D0(_5),
    .D1(_6), .D2(_7), .D3(_8));
  not not_1 (not_1_out, nLb);
  BufferRegister bufferregister_2 (
    .LOAD(not_2_out), .CLK(CLK), .CLR(1'b0), .ENABLE(1'b1), .X0(D1), .X1(D2), .X2(D3), .X3(D4), .D0(_1),
    .D1(_2), .D2(_3), .D3(_4));
  not not_2 (not_2_out, nLb);
endmodule

module Adder_subtractor (
  input  b4,
  input  a4,
  input  b3,
  input  a3,
  input  b2,
  input  a2,
  input  b1,
  input  a1,
  input  in_9,
  output out_10,
  output out_11,
  output out_12,
  output out_13,
  output out_14
);

  wire adder_1_cout, adder_2_cout, adder_3_cout;

  Adder #(.width(1)) adder_1 (.a(a4), .b(b4), .out(out_10), .cin(in_9), .cout(adder_1_cout));
  Adder #(.width(1)) adder_2 (.a(a3), .b(b3), .out(out_11), .cin(adder_1_cout), .cout(adder_2_cout));
  Adder #(.width(1)) adder_3 (.a(a2), .b(b2), .out(out_12), .cin(adder_2_cout), .cout(adder_3_cout));
  Adder #(.width(1)) adder_4 (.a(a1), .b(b1), .out(out_13), .cin(adder_3_cout), .cout(out_14));
endmodule
